// Logisim project workdesign.circ as structural Verilog: 12 circuits, main circuit main
module main (
);

  wire button_1_out, button_2_out, decoder_1_out15;
  wire [3:0] model3_1_car_pos, model8_1_scan;
  wire [15:0] decoder_2_out0, not_1_out;

  Button button_1 (.out(button_1_out));
  Button button_2 (.out(button_2_out));
  model8 model8_1 (.SCAN(model8_1_scan));  // open: CAR, OBS
  Decoder #(.select(4)) decoder_1 (
    .out0(not_1_out[15]), .out1(not_1_out[14]), .out2(not_1_out[13]), .out3(not_1_out[12]),
    .out4(not_1_out[11]), .out5(not_1_out[10]), .out6(not_1_out[9]), .out7(not_1_out[8]),
    .out8(not_1_out[7]), .out9(not_1_out[6]), .out10(not_1_out[5]), .out11(not_1_out[4]),
    .out12(not_1_out[3]), .out13(not_1_out[2]), .out14(not_1_out[1]), .out15(decoder_1_out15),
    .sel(model8_1_scan));  // open: en
  model3 model3_1 (.LEFT(button_1_out), .RIGHT(button_2_out), .car_pos(model3_1_car_pos));  // open: Reset
  Decoder #(.select(4)) decoder_2 (
    .out0(decoder_2_out0[0]), .out1(decoder_2_out0[1]), .out2(decoder_2_out0[2]), .out3(decoder_2_out0[3]),
    .out4(decoder_2_out0[4]), .out5(decoder_2_out0[5]), .out6(decoder_2_out0[6]), .out7(decoder_2_out0[7]),
    .out8(decoder_2_out0[8]), .out9(decoder_2_out0[9]), .out10(decoder_2_out0[10]),
    .out11(decoder_2_out0[11]), .out12(decoder_2_out0[12]), .out13(decoder_2_out0[13]),
    .out14(decoder_2_out0[14]), .out15(decoder_2_out0[15]), .sel(model3_1_car_pos));  // open: en
  not not_1 (not_1_out[0], decoder_1_out15);
  // DotMatrix #(.inputtype("select"), .matrixcols(16), .matrixrows(16)) dotmatrix_1: pin names not known; wires that end beside it: decoder_2_out0, not_1_out
endmodule

module Input_system (
  input  SPEED0,
  input  SPEED1
);

  Clock CLK ();  // open: out
  Button LEFT ();  // open: out
  Button RIGHT ();  // open: out
  Button START ();  // open: out
  Button RST ();  // open: out
endmodule

module module1 (
  input  [1:0] in_1,
  output [3:0] out_2
);

  wire clock_1_out;
  wire [3:0] adder_1_out, adder_2_out, adder_3_out, CNT1_q, CNT2_q, CNT3_q;

  Clock clock_1 (.out(clock_1_out));
  Adder #(.width(4)) adder_1 (.a(CNT1_q), .b(4'b0001), .out(adder_1_out));  // open: cin, cout
  Adder #(.width(4)) adder_2 (.a(CNT1_q), .b(CNT1_q), .out(adder_2_out));  // open: cin, cout
  Adder #(.width(4)) adder_3 (.a(CNT2_q), .b(CNT1_q), .out(adder_3_out));  // open: cin, cout
  Register #(.width(4)) CNT1 (.D(adder_1_out), .clk(clock_1_out), .Q(CNT1_q));  // open: en, clr
  Register #(.width(4)) CNT2 (.D(adder_2_out), .clk(clock_1_out), .Q(CNT2_q));  // open: en, clr
  Register #(.width(4)) CNT3 (.D(adder_3_out), .clk(clock_1_out), .Q(CNT3_q));  // open: en, clr
  Multiplexer #(.select(2), .width(4)) multiplexer_1 (
    .in1(CNT1_q), .in2(CNT2_q), .in3(CNT3_q), .out(out_2), .sel(in_1));  // open: in0
endmodule

module model2 (
  output [3:0] SRC_PIN
);

  wire clock_1_out;
  wire [3:0] adder_1_out;

  Clock clock_1 (.out(clock_1_out));
  Register #(.width(4)) OBS_SRC (.D(adder_1_out), .clk(clock_1_out), .Q(SRC_PIN));  // open: en, clr
  Adder #(.width(4)) adder_1 (.a(SRC_PIN), .b(4'b0011), .out(adder_1_out));  // open: cin, cout
endmodule

module model3 (
  input  LEFT,
  input  RIGHT,
  input  Reset,
  output [3:0] car_pos
);

  wire clock_1_out, comparator_1_gt, comparator_1_lt, comparator_2_gt, comparator_2_lt, or_1_out, or_2_out;
  wire [1:0] and_2_out;
  wire [3:0] adder_1_out, multiplexer_1_out;

  Multiplexer #(.select(2), .width(4)) multiplexer_1 (
    .in0(4'b0000), .in1(4'b1111), .in2(4'b0001), .in3(4'b0000), .out(multiplexer_1_out), .sel(and_2_out));
  Clock clock_1 (.out(clock_1_out));
  Adder #(.width(4)) adder_1 (.a(multiplexer_1_out), .b(car_pos), .out(adder_1_out));  // open: cin, cout
  Register #(.width(4)) register_1 (.D(adder_1_out), .clk(clock_1_out), .Q(car_pos), .clr(Reset));  // open: en
  Comparator #(.width(4)) comparator_1 (
    .a(car_pos), .b(4'b0000), .gt(comparator_1_gt), .lt(comparator_1_lt));  // open: eq
  Comparator #(.width(4)) comparator_2 (
    .a(car_pos), .b(4'b1111), .gt(comparator_2_gt), .lt(comparator_2_lt));  // open: eq
  or or_1 (or_1_out, comparator_1_gt, comparator_1_lt);
  or or_2 (or_2_out, comparator_2_gt, comparator_2_lt);
  and and_1 (and_2_out[1], or_2_out, RIGHT);
  and and_2 (and_2_out[0], LEFT, or_1_out);
endmodule

module model4 (
  input  [3:0] OBS_SRC,
  input  Reset,
  output [3:0] out_3,
  output out_4
);

  wire clock_1_out;
  wire [3:0] adder_1_out, OBS_COL_q;

  Clock clock_1 (.out(clock_1_out));
  Register #(.width(4)) OBS_COL (.D(OBS_SRC), .en(clock_1_out), .clk(clock_1_out), .Q(OBS_COL_q), .clr(Reset));
  Register #(.width(4)) OBS_ROW (.D(adder_1_out), .en(clock_1_out), .clk(clock_1_out), .Q(out_3), .clr(Reset));
  Adder #(.width(4)) adder_1 (.a(OBS_COL_q), .b(4'b0001), .out(adder_1_out));  // open: cin, cout
  Comparator #(.width(4)) comparator_1 (.a(out_3), .b(4'b1111), .eq(out_4));  // open: gt, lt
endmodule

module model5 (
  input  [3:0] in_1,
  input  [3:0] in_2,
  input  At_Botton,
  output hit
);

  wire comparator_1_eq;

  Comparator #(.width(4)) comparator_1 (.a(in_1), .b(in_2), .eq(comparator_1_eq));  // open: gt, lt
  and and_1 (hit, comparator_1_eq, At_Botton);
endmodule

module model6 (
  input  HIT,
  output RUN,
  output GRN,
  output RED
);

  wire and_1_out, clock_1_out, KEEP_out, not_1_out, not_2_out, not_3_out, S0_out, START_out;

  Clock clock_1 (.out(clock_1_out));
  not not_1 (not_1_out, HIT);
  and and_1 (and_1_out, RED, not_1_out);
  and KEEP (KEEP_out, HIT, RED);
  or S0 (S0_out, START_out, and_1_out);
  D_Flip_Flop FF_S1 (.D(KEEP_out), .clk(clock_1_out), .Q(GRN));  // open: Qn, preset, reset
  D_Flip_Flop FF_S0 (.D(S0_out), .clk(clock_1_out), .Q(RED));  // open: Qn, preset, reset
  not not_2 (not_2_out, GRN);
  not not_3 (not_3_out, RED);
  and START (START_out, not_2_out, not_3_out);

  assign RUN = HIT;
endmodule

module model7 (
  input  AT_BOTTOM,
  input  HIT,
  input  RUNNING,
  output [3:0] SCORE1_Q,
  output [3:0] SCORE10_Q
);

  wire clock_1_out, comparator_1_eq, SCORE_out;
  wire [3:0] adder_1_out, adder_2_out, multiplexer_1_out;

  Clock clock_1 (.out(clock_1_out));
  Register #(.width(4)) SCORE1 (.D(adder_1_out), .en(SCORE_out), .clk(clock_1_out), .Q(SCORE1_Q));  // open: clr
  Register #(.width(4)) SCORE10 (.D(adder_2_out), .en(comparator_1_eq), .clk(clock_1_out), .Q(SCORE10_Q));  // open: clr
  Adder #(.width(4)) adder_1 (.a(4'b0001), .b(SCORE1_Q), .out(adder_1_out));  // open: cin, cout
  Multiplexer #(.width(4)) multiplexer_1 (.in0(4'b0000), .in1(4'b0001), .out(multiplexer_1_out), .sel(comparator_1_eq));
  and SCORE (SCORE_out, AT_BOTTOM, HIT, RUNNING);
  Adder #(.width(4)) adder_2 (.a(SCORE10_Q), .b(multiplexer_1_out), .out(adder_2_out));  // open: cin, cout
  // NOT_Gate not_1 is placed but not wired
  Comparator #(.width(4)) comparator_1 (.a(SCORE1_Q), .b(4'b1001), .eq(comparator_1_eq));  // open: gt, lt
endmodule

module model8 (
  input  CAR,
  input  [3:0] OBS,
  output [3:0] SCAN
);

  wire clock_1_out, comparator_1_gt, comparator_1_lt, decoder_1_out0, decoder_1_out1, decoder_1_out2,
       decoder_1_out3, decoder_1_out4, decoder_1_out5, decoder_1_out6, decoder_1_out7, decoder_1_out8,
       decoder_1_out9, decoder_1_out10, decoder_1_out11, decoder_1_out12, decoder_1_out13, decoder_1_out14,
       decoder_1_out15, or_1_out;
  wire [3:0] adder_1_out, multiplexer_1_out;

  Clock clock_1 (.out(clock_1_out));
  Register #(.width(4)) SCAN_ROW (.D(multiplexer_1_out), .clk(clock_1_out), .Q(SCAN));  // open: en, clr
  Decoder #(.select(4)) decoder_1 (
    .out0(decoder_1_out0), .out1(decoder_1_out1), .out2(decoder_1_out2), .out3(decoder_1_out3),
    .out4(decoder_1_out4), .out5(decoder_1_out5), .out6(decoder_1_out6), .out7(decoder_1_out7),
    .out8(decoder_1_out8), .out9(decoder_1_out9), .out10(decoder_1_out10), .out11(decoder_1_out11),
    .out12(decoder_1_out12), .out13(decoder_1_out13), .out14(decoder_1_out14), .out15(decoder_1_out15),
    .sel(SCAN), .en(CAR));
  DotMatrix #(.inputtype("row"), .matrixcols(1), .matrixrows(16)) LED_Matrix (
    .row0(decoder_1_out0), .row1(decoder_1_out1), .row2(decoder_1_out2), .row3(decoder_1_out3),
    .row4(decoder_1_out4), .row5(decoder_1_out5), .row6(decoder_1_out6), .row7(decoder_1_out7),
    .row8(decoder_1_out8), .row9(decoder_1_out9), .row10(decoder_1_out10), .row11(decoder_1_out11),
    .row12(decoder_1_out12), .row13(decoder_1_out13), .row14(decoder_1_out14), .row15(decoder_1_out15));
  Adder #(.width(4)) adder_1 (.a(SCAN), .b(4'b0001), .out(adder_1_out));  // open: cin, cout
  Comparator #(.width(4)) comparator_1 (
    .a(adder_1_out), .b(4'b1111), .gt(comparator_1_gt), .lt(comparator_1_lt));  // open: eq
  Comparator #(.width(4)) comparator_2 (.a(SCAN), .b(4'b1110));  // open: gt, eq, lt
  Comparator #(.width(4)) comparator_3 (.a(SCAN), .b(4'b1111));  // open: gt, eq, lt
  Comparator #(.width(4)) comparator_4 (.a(SCAN), .b(OBS));  // open: gt, eq, lt
  Multiplexer #(.width(4)) multiplexer_1 (.in0(4'b0000), .in1(adder_1_out), .out(multiplexer_1_out), .sel(or_1_out));
  or or_1 (or_1_out, comparator_1_gt, comparator_1_lt);
endmodule

module Output_system (
);

  LED GRN ();  // open: in
  LED RED ();  // open: in
  // Buzzer buzzer_1: pin names not known
  _7_Segment_Display u_7_segment_display_1 ();  // open: g, f, a, b, e, d, c, dp
  _7_Segment_Display u_7_segment_display_2 ();  // open: g, f, a, b, e, d, c, dp
endmodule

module LED_TEST (
);

  // DotMatrix #(.inputtype("select"), .matrixcols(16), .matrixrows(16)) dotmatrix_1: pin names not known
endmodule
